# Fritzing sketch Embedded Examen - Greenhouse (saved by Fritzing 0.9.10b)
breadboards: 1

parts:
  Part1 = Adafruit ESP32-S3 Feather [part_number="Adafruit #5323"]
  ZS-042_RTC1 = ZS-042 RTC Module
  IC1 = L293D [package=THT]
  M1 = DC Motor [voltage_(max)=6V voltage_(min)=3V]
  MOTOR2 = 28BYJ-48 Stepper Motor  # not connected
  ULN2003AN_used_in_project = 28BYJ-48 Driver Module [part_number=ULN2003 package=THT]

nets:
  GND: Part1.GND, Part1.A2, ZS-042_RTC1.GND, IC1.0V, M1.pin_1, ULN2003AN_used_in_project.GND
  N1: Part1.VBUS, ZS-042_RTC1.VCC, IC1.+Vmotor, IC1.+V, ULN2003AN_used_in_project.Vmotor
  N2: Part1.D12, ULN2003AN_used_in_project.IN4
  N3: Part1.D11, ULN2003AN_used_in_project.IN3
  N4: Part1.D10, ULN2003AN_used_in_project.IN2
  N5: Part1.D9, ULN2003AN_used_in_project.IN1
  N6: Part1.D6, IC1.In_1
  N7: Part1.D5, IC1.Enable_1
  N8: Part1.SCL, ZS-042_RTC1.SCL
  N9: Part1.SDA, ZS-042_RTC1.SDA
  N10: IC1.Out_1_(_Controlled_by_Enable_1_), M1.pin_2

custom parts:
  Adafruit ESP32-S3 Feather: The ESP32-S3 has arrived in Feather format - and what a great way to get started with this powerful new chip from Espressif! With dual 240 MHz cores, WiFi and BLE support, and native USB, this Feather is great for powering your IoT projects. That's right - it's the new Adafruit ESP32-S3 Feather! With native USB and 8 MB flash, this board will let you upgrade your existing ESP32 projects.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
  28BYJ-48 Driver Module: Generic male header
